// Logisim project serial_adder.circ as structural Verilog: 1 circuit, main circuit main
module main (
  input  Clear,
  output s3,
  output s2,
  output s1,
  output s0
);

  wire adder_1_cout, adder_1_out, Clock__tap_8_times_out, d_ff_1_q, d_ff_2_q, d_ff_3_q, d_ff_4_q, d_ff_5_q,
       d_ff_6_q, d_ff_7_q, d_ff_8_q, d_ff_9_q;

  Clock Clock__tap_8_times (.out(Clock__tap_8_times_out));
  D_Flip_Flop d_ff_1 (.clk(Clock__tap_8_times_out), .D(1'b0), .Q(d_ff_1_q), .reset(Clear));  // open: Qn, preset, en
  D_Flip_Flop d_ff_2 (.clk(Clock__tap_8_times_out), .D(1'b0), .Q(d_ff_2_q), .reset(Clear));  // open: Qn, preset, en
  D_Flip_Flop d_ff_3 (.clk(Clock__tap_8_times_out), .D(d_ff_1_q), .Q(d_ff_3_q), .reset(Clear));  // open: Qn, preset, en
  D_Flip_Flop d_ff_4 (.clk(Clock__tap_8_times_out), .D(d_ff_2_q), .Q(d_ff_4_q), .reset(Clear));  // open: Qn, preset, en
  D_Flip_Flop d_ff_5 (.clk(Clock__tap_8_times_out), .D(d_ff_3_q), .Q(d_ff_5_q), .reset(Clear));  // open: Qn, preset, en
  D_Flip_Flop d_ff_6 (.clk(Clock__tap_8_times_out), .D(d_ff_4_q), .Q(d_ff_6_q), .reset(Clear));  // open: Qn, preset, en
  D_Flip_Flop d_ff_7 (.clk(Clock__tap_8_times_out), .D(d_ff_5_q), .Q(d_ff_7_q), .reset(Clear));  // open: Qn, preset, en
  D_Flip_Flop d_ff_8 (.clk(Clock__tap_8_times_out), .D(d_ff_6_q), .Q(d_ff_8_q), .reset(Clear));  // open: Qn, preset, en
  Adder #(.width(1)) adder_1 (.a(d_ff_7_q), .b(d_ff_8_q), .out(adder_1_out), .cin(d_ff_9_q), .cout(adder_1_cout));
  D_Flip_Flop d_ff_9 (
    .clk(Clock__tap_8_times_out), .D(adder_1_cout), .Q(d_ff_9_q), .reset(Clear));  // open: Qn, preset, en
  D_Flip_Flop d_ff_10 (.clk(Clock__tap_8_times_out), .D(adder_1_out), .Q(s3), .reset(Clear));  // open: Qn, preset, en
  D_Flip_Flop d_ff_11 (.clk(Clock__tap_8_times_out), .D(s3), .Q(s2), .reset(Clear));  // open: Qn, preset, en
  D_Flip_Flop d_ff_12 (.clk(Clock__tap_8_times_out), .D(s2), .Q(s1), .reset(Clear));  // open: Qn, preset, en
  D_Flip_Flop d_ff_13 (.clk(Clock__tap_8_times_out), .D(s1), .Q(s0), .reset(Clear));  // open: Qn, preset, en

  // Notes on the sheet:
  //   A
  //   B
endmodule
