// Logisim project Pratica01-CircuitosCombinacionais.circ as structural Verilog: 1 circuit, main circuit main
module main (
  input  in_1,
  input  a,
  input  b,
  input  b_2,
  input  a_2,
  input  b_3,
  input  sel,
  input  a_3,
  input  b_4,
  input  a_4,
  input  a_5,
  input  b_5,
  output out_13,
  output out_14,
  output out_15,
  output out_16,
  output out_17,
  output out_18
);

  wire adder_1_cout, adder_2_cout, adder_3_cout, and_1_out, and_2_out;

  and and_1 (and_1_out, b_2, sel);
  and and_2 (and_2_out, ~sel, a_4);  // AND_Gate
  or or_1 (out_15, and_1_out, and_2_out);
  Adder #(.width(1)) adder_1 (.a(a), .b(b), .out(out_13), .cin(in_1), .cout(adder_1_cout));
  Adder #(.width(1)) adder_2 (.a(a_2), .b(b_3), .out(out_14), .cin(adder_1_cout), .cout(adder_2_cout));
  Adder #(.width(1)) adder_3 (.a(a_3), .b(b_4), .out(out_16), .cin(adder_2_cout), .cout(adder_3_cout));
  Adder #(.width(1)) adder_4 (.a(a_5), .b(b_5), .out(out_17), .cin(adder_3_cout), .cout(out_18));
endmodule
